# Fritzing sketch planeur (saved by Fritzing 1.0.6)
breadboards: 1

parts:
  Composant1 = Arduino Micro (Rev3)
  MCU1 = Raspberry Pi Zero
  Composant2 = Adafruit ICM20948  # not connected
  U1 = VK2828U7G5LF
  BAT1 = Battery Holders [package=lipo-1100mAh]
  Composant3 = PowerBoost 500 Charger

nets:
  GND: Composant1.D1/TX, MCU1.pin_5, MCU1.pin_6, MCU1.pin_9, MCU1.pin_10, MCU1.pin_13, MCU1.pin_14, MCU1.pin_19, MCU1.pin_20, MCU1.pin_25, MCU1.pin_26, MCU1.pin_29, MCU1.pin_30, MCU1.pin_33, MCU1.pin_34, MCU1.pin_39, MCU1.pin_40, U1.GND, BAT1.-, Composant3.GND
  N1: Composant1.D0/RX, MCU1.pin_7, MCU1.pin_8
  N2: MCU1.pin_1, MCU1.pin_2, MCU1.pin_3, MCU1.pin_4, MCU1.pin_17, MCU1.pin_18, U1.TX, U1.VCC, Composant3.5.0V
  N3: MCU1.pin_11, MCU1.pin_12, U1.EN
  N4: MCU1.pin_15, MCU1.pin_16, U1.RX
  N5: MCU1.pin_21, MCU1.pin_22
  N6: MCU1.pin_23, MCU1.pin_24
  N7: MCU1.pin_27, MCU1.pin_28
  N8: MCU1.pin_31, MCU1.pin_32
  N9: MCU1.pin_35, MCU1.pin_36
  N10: MCU1.pin_37, MCU1.pin_38
  N11: BAT1.+, Composant3.VBAT_OUT

notes:
  +3.3V
  +5V
  RX
  TX

custom parts:
  VK2828U7G5LF: VK2828U7G5LF GPS
